# Fritzing sketch Breadboard (saved by Fritzing 0.8.3b)
breadboards: 1

parts:
  U1 = ESP8266 WiFi Module [part_number=ESP8266]
  S1 = Pushbutton [package="[THT]"]
  C1 = Electrolytic Capacitor [capacitance=1µF package="100 mil [THT, electrolytic]"]
  Part1 = Arduino Uno (Rev3)
  R1 = Resistor [tolerance=±5% resistance=220 package=THT]
  R2 = Resistor [tolerance=±5% resistance=220 package=THT]
  R3 = Resistor [tolerance=±5% resistance=220 package=THT]
  S2 = Pushbutton [package="[THT]"]

nets:
  N1: U1.RXD, R1.Pin_0, R2.Pin_0
  N2: U1.VCC, U1.CH_PD, C1.+, R3.Pin_1, S2.Pin_1, S2.Pin_2
  N3: U1.GPIO_0, U1.RST, S1.Pin_1, S1.Pin_2
  N4: U1.GPIO_2, R3.Pin_0
  GND: U1.GND, S1.Pin_3, S1.Pin_4, C1.-, Part1.GND, Part1.RESET, R1.Pin_1
  N5: U1.TXD, Part1.D1/TX
  N6: Part1.D0/RX, R2.Pin_1
  N7: Part1.3V3, S2.Pin_3, S2.Pin_4

custom parts:
  ESP8266 WiFi Module: Generic WiFi Module based on the ESP8266 with onboard PCB antenna and UART communications
