# Fritzing sketch GettingStarted (saved by Fritzing 0.8.3b)
breadboards: 1

parts:
  U1 = ESP8266 WiFi Module [part_number=ESP8266]
  R1 = Resistor [tolerance=±5% resistance=220 package=THT]
  LED1 = LED - 5mm [color="Red (633nm)" package="5 mm [THT]"]
  S1 = Pushbutton [package="[THT]"]
  Part1 = FTDI Basic Programmer
  R2 = Resistor [tolerance=±5% resistance=4.7k package=THT]

nets:
  N1: U1.RXD, Part1.TXO
  N2: U1.VCC, U1.CH_PD, Part1.POWER, R2.Pin_1
  N3: U1.GPIO_0, U1.RST, S1.Pin_1, S1.Pin_2
  N4: U1.GPIO_2, R1.Pin_0, R2.Pin_0
  GND: U1.GND, LED1.cathode, S1.Pin_3, S1.Pin_4, Part1.GND
  N5: U1.TXD, Part1.RXI
  N6: R1.Pin_1, LED1.anode

custom parts:
  ESP8266 WiFi Module: Generic WiFi Module based on the ESP8266 with onboard PCB antenna and UART communications
