# Fritzing sketch Breadboard (saved by Fritzing 0.8.3b)
breadboards: 1

parts:
  U1 = ESP8266 WiFi Module [part_number=ESP8266]
  R1 = Resistor [tolerance=±5% resistance=220 package=THT]
  R2 = Resistor [tolerance=±5% resistance=4.7k package=THT]
  LED1 = LED - 5mm [color="Red (633nm)" package="5 mm [THT]"]
  Power_plug1 = Power plug

nets:
  VCC: U1.VCC, U1.CH_PD, R2.Pin_1, Power_plug1.VCC
  N1: U1.GPIO_2, R1.Pin_1, R2.Pin_0
  GND: U1.GND, LED1.cathode, Power_plug1.GND
  N2: R1.Pin_0, LED1.anode

notes:
  3.3V Power

custom parts:
  ESP8266 WiFi Module: Generic WiFi Module based on the ESP8266 with onboard PCB antenna and UART communications
