# Fritzing sketch Both on one breadboard (saved by Fritzing 0.8.3b)
breadboards: 1

parts:
  U1 = ESP8266 WiFi Module [part_number=ESP8266]
  R2 = Resistor [tolerance=±5% resistance=4.7k package=THT]
  Power_plug1 = Power plug
  R1 = Resistor [tolerance=±5% resistance=220 package=THT]
  U2 = TLP621 [package=THT]
  Power_plug2 = Power plug
  C1 = Electrolytic Capacitor [capacitance=1µF package="100 mil [THT, electrolytic]"]  # not connected
  KY-1 = Keyes Relay [package=THT]
  U3 = ESP8266 WiFi Module [part_number=ESP8266]
  R3 = Resistor [tolerance=±5% resistance=220 package=THT]
  S1 = Pushbutton [package="[THT]"]

nets:
  VCC: U1.VCC, U1.RST, U1.CH_PD, R2.Pin_1, Power_plug1.VCC, U3.VCC, U3.CH_PD, R3.Pin_1
  N1: U1.GPIO_0, U1.GPIO_2, R2.Pin_0, R1.Pin_1
  GND: U1.GND, Power_plug1.GND, U2.Pin_1, U3.GND, S1.Pin_3, S1.Pin_4
  N2: R1.Pin_0, U2.Pin_2
  N3: U2.Pin_4, Power_plug2.VCC, KY-1.power
  N4: U2.Pin_3, KY-1.signal
  N5: Power_plug2.GND, KY-1.ground
  N6: U3.GPIO_0, U3.GPIO_2, R3.Pin_0, S1.Pin_1, S1.Pin_2

notes:
  3.3V Power

custom parts:
  ESP8266 WiFi Module: Generic WiFi Module based on the ESP8266 with onboard PCB antenna and UART communications
  Keyes Relay: The Keyes 5V relay module is suitable for SCM development, home appliance control. It uses a 5V~12V TIL control signal which can control DC / AC signal.
