# Fritzing sketch Button Board (saved by Fritzing 0.8.3b)
breadboards: 1

parts:
  U1 = ESP8266 WiFi Module [part_number=ESP8266]
  R2 = Resistor [tolerance=±5% resistance=4.7k package=THT]
  Power_plug1 = Power plug
  S1 = Pushbutton [package="[THT]"]

nets:
  VCC: U1.VCC, U1.CH_PD, R2.Pin_1, Power_plug1.VCC
  N1: U1.GPIO_2, R2.Pin_0, S1.Pin_1, S1.Pin_2
  GND: U1.GND, Power_plug1.GND, S1.Pin_3, S1.Pin_4

notes:
  3.3V Power

custom parts:
  ESP8266 WiFi Module: Generic WiFi Module based on the ESP8266 with onboard PCB antenna and UART communications
