# Fritzing sketch Relay Board (saved by Fritzing 0.8.3b)
breadboards: 1

parts:
  U1 = ESP8266 WiFi Module [part_number=ESP8266]
  R1 = Resistor [tolerance=±5% resistance=220 package=THT]
  R2 = Resistor [tolerance=±5% resistance=4.7k package=THT]
  Power_plug1 = Power plug
  KY-1 = Keyes Relay [package=THT]
  U2 = TLP621 [package=THT]
  Power_plug2 = Power plug
  C1 = Electrolytic Capacitor [capacitance=1µF package="100 mil [THT, electrolytic]"]  # not connected

nets:
  VCC: U1.VCC, U1.CH_PD, R2.Pin_1, Power_plug1.VCC
  N1: U1.GPIO_2, R1.Pin_1, R2.Pin_0
  GND: U1.GND, Power_plug1.GND, U2.Pin_1
  N2: R1.Pin_0, U2.Pin_2
  N3: KY-1.signal, U2.Pin_3
  N4: KY-1.power, U2.Pin_4, Power_plug2.VCC
  N5: KY-1.ground, Power_plug2.GND

notes:
  3.3V Power
  5V Power

custom parts:
  ESP8266 WiFi Module: Generic WiFi Module based on the ESP8266 with onboard PCB antenna and UART communications
  Keyes Relay: The Keyes 5V relay module is suitable for SCM development, home appliance control. It uses a 5V~12V TIL control signal which can control DC / AC signal.
