# Fritzing sketch ESP Nodes (saved by Fritzing 0.8.3b)
breadboards: 1

parts:
  U1 = ESP8266 WiFi Module [part_number=ESP8266]
  Power_plug1 = Power plug
  C1 = Electrolytic Capacitor [capacitance=1µF package="100 mil [THT, electrolytic]"]
  U3 = ESP8266 WiFi Module [part_number=ESP8266]
  R3 = Resistor [tolerance=±5% resistance=220 package=THT]
  DS1 = DS18B20 1-Wire Temperature Sensor [part_number=DS18B20]
  R4 = Resistor [tolerance=±5% resistance=4.7k package=THT]
  S1 = Reed switch [package=THT]

nets:
  VCC: U1.VCC, U1.RST, U1.CH_PD, Power_plug1.VCC, C1.+, U3.VCC, U3.CH_PD, R3.Pin_1, DS1.VDD, R4.Pin_1, S1.pin_2
  N1: U1.GPIO_0, U1.GPIO_2, DS1.DQ, R4.Pin_0
  GND: U1.GND, Power_plug1.GND, C1.-, U3.GND, DS1.GND, S1.pin_1
  N2: U3.GPIO_0, U3.GPIO_2, R3.Pin_0

notes:
  3.3V Power

custom parts:
  ESP8266 WiFi Module: Generic WiFi Module based on the ESP8266 with onboard PCB antenna and UART communications
