# Fritzing sketch Teensy Monitor (saved by Fritzing 0.8.3b)
breadboards: 1

parts:
  R3 = Resistor [tolerance=±5% resistance=220 package=THT]
  LED4 = LED - 5mm [color="Red (633nm)" package="5 mm [THT]"]
  R1 = Resistor [tolerance=±5% resistance=220 package=THT]
  R4 = Resistor [tolerance=±5% resistance=220 package=THT]
  R2 = Resistor [tolerance=±5% resistance=220 package=THT]
  U1 = ESP8266 WiFi Module [part_number=ESP8266]
  LED1 = LED - 5mm [color="Blue (430nm)" package="5 mm [THT]"]
  LED2 = LED - 5mm [color="Green (555nm)" package="5 mm [THT]"]
  LED3 = LED - 5mm [color="Red (633nm)" package="5 mm [THT]"]
  Teensy1 = Teensy 2.0

nets:
  GND: R3.Pin_0, R2.Pin_1, U1.GND, Teensy1.GND
  N1: R3.Pin_1, LED2.cathode
  N2: LED4.cathode, R2.Pin_0
  N3: LED4.anode, Teensy1.C7
  N4: R1.Pin_1, LED1.cathode
  N5: R4.Pin_1, LED3.cathode, Teensy1.B5
  N6: U1.RXD, Teensy1.D3
  VCC: U1.VCC, U1.GPIO_2, U1.CH_PD, Teensy1.VCC
  N7: U1.TXD, Teensy1.D2
  N8: LED1.anode, Teensy1.D7
  N9: LED2.anode, Teensy1.B4

custom parts:
  ESP8266 WiFi Module: Generic WiFi Module based on the ESP8266 with onboard PCB antenna and UART communications
  Teensy 2.0: The Teensy is a complete USB-based microcontoller development system, in a very small footprint, capable of implementing many types of projects. All programming is done via the USB port. No special programmer is needed, only a standard "Mini-B" USB cable and a PC or Macintosh with a USB port.
