# Fritzing sketch ESP Nodes (saved by Fritzing 0.8.3b)
breadboards: 2

parts:
  U1 = ESP8266 WiFi Module [part_number=ESP8266]
  Power_plug1 = Power plug
  C1 = Electrolytic Capacitor [capacitance=1µF package="100 mil [THT, electrolytic]"]
  U3 = ESP8266 WiFi Module [part_number=ESP8266]
  R3 = Resistor [tolerance=±5% resistance=220 package=THT]
  DS1 = DS18B20 1-Wire Temperature Sensor [part_number=DS18B20]
  R4 = Resistor [tolerance=±5% resistance=4.7k package=THT]
  S1 = Reed switch [package=THT]
  Power_plug2 = Power plug
  U4 = ESP8266 WiFi Module [part_number=ESP8266]
  U5 = TLP621 [package=THT]
  R5 = Resistor [tolerance=±5% resistance=220 package=THT]
  R6 = Resistor [tolerance=±5% resistance=220 package=THT]
  KY-1 = Keyes Relay [package=THT]

nets:
  VCC: U1.VCC, U1.RST, U1.CH_PD, U1.TXD, Power_plug1.VCC, C1.+, U3.VCC, U3.RST, U3.CH_PD, U3.TXD, R3.Pin_1, DS1.VDD, R4.Pin_1, S1.pin_2, U4.VCC, U4.CH_PD, R6.Pin_1
  N1: U1.GPIO_0, U1.GPIO_2, DS1.DQ, R4.Pin_0
  GND: U1.GND, Power_plug1.GND, C1.-, U3.GND, DS1.GND, S1.pin_1, U4.GND, U5.Pin_2
  N2: U3.GPIO_0, U3.GPIO_2, R3.Pin_0
  N3: Power_plug2.VCC, U5.Pin_3, KY-1.power
  N4: Power_plug2.GND, KY-1.ground
  N5: U4.GPIO_2, R5.Pin_1, R6.Pin_0
  N6: U5.Pin_1, R5.Pin_0
  N7: U5.Pin_4, KY-1.signal

notes:
  3.3V Power
  5V Power
  Light Node
  Door Node
  Temperature Node

custom parts:
  ESP8266 WiFi Module: Generic WiFi Module based on the ESP8266 with onboard PCB antenna and UART communications
  Keyes Relay: The Keyes 5V relay module is suitable for SCM development, home appliance control. It uses a 5V~12V TIL control signal which can control DC / AC signal.
