# Fritzing sketch Teensy Monitor (saved by Fritzing 0.8.3b)
breadboards: 1

parts:
  Teensy1 = Teensy 2.0
  U1 = ESP8266 WiFi Module [part_number=ESP8266]
  R1 = Resistor [tolerance=±5% resistance=220 package=THT]
  R2 = Resistor [tolerance=±5% resistance=220 package=THT]
  R3 = Resistor [tolerance=±5% resistance=220 package=THT]
  R4 = Resistor [tolerance=±5% resistance=220 package=THT]
  LED1 = LED - 5mm [color="Blue (430nm)" package="5 mm [THT]"]
  LED2 = LED - 5mm [color="Green (555nm)" package="5 mm [THT]"]
  LED3 = LED - 5mm [color="Red (633nm)" package="5 mm [THT]"]
  LED4 = LED - 5mm [color="Red (633nm)" package="5 mm [THT]"]
  R5 = Resistor [tolerance=±5% resistance=220 package=THT]
  LED5 = LED - 5mm [color="White (6500K)" package="5 mm [THT]"]
  R6 = Resistor [tolerance=±5% resistance=220 package=THT]
  R7 = Resistor [tolerance=±5% resistance=220 package=THT]
  R8 = Resistor [tolerance=±5% resistance=220 package=THT]
  LED6 = LED - 5mm [color="Red (633nm)" package="5 mm [THT]"]
  LED7 = LED - 5mm [color="Yellow (592nm)" package="5 mm [THT]"]
  LED8 = LED - 5mm [color="Green (555nm)" package="5 mm [THT]"]

nets:
  GND: Teensy1.GND, U1.GND, R2.Pin_1, R3.Pin_0, R5.Pin_1, R6.Pin_1, R7.Pin_1, R8.Pin_1
  N1: Teensy1.B7, LED6.anode
  N2: Teensy1.D0, LED7.anode
  N3: Teensy1.D1, LED8.anode
  N4: Teensy1.D2, U1.TXD
  N5: Teensy1.D3, U1.RXD
  N6: Teensy1.C6, LED5.anode
  N7: Teensy1.C7, LED4.anode
  N8: Teensy1.D7, LED1.anode
  N9: Teensy1.B4, LED2.anode
  N10: Teensy1.B5, R4.Pin_1, LED3.cathode
  VCC: Teensy1.VCC, U1.VCC, U1.CH_PD
  N11: R1.Pin_1, LED1.cathode
  N12: R2.Pin_0, LED4.cathode
  N13: R3.Pin_1, LED2.cathode
  N14: R5.Pin_0, LED5.cathode
  N15: R6.Pin_0, LED8.cathode
  N16: R7.Pin_0, LED7.cathode
  N17: R8.Pin_0, LED6.cathode

notes:
  Note that the wiring for the ESP8266 is incomplete here - it should have it's own 3.3v power and the serial logic needs to be brought to 3.3v as well. I just dont have the breakout board in Fritzing to show that.
  Temperature
  <- Door | Light ->
  <- Security

custom parts:
  Teensy 2.0: The Teensy is a complete USB-based microcontoller development system, in a very small footprint, capable of implementing many types of projects. All programming is done via the USB port. No special programmer is needed, only a standard "Mini-B" USB cable and a PC or Macintosh with a USB port.
  ESP8266 WiFi Module: Generic WiFi Module based on the ESP8266 with onboard PCB antenna and UART communications
