# Fritzing sketch RGBlight (saved by Fritzing 0.8.3b)

parts:
  U1 = ESP8266 WiFi Module [part_number=ESP8266]
  U2 = Voltage Regulator [package=to220-adj]
  R1 = Resistor [tolerance=±5% resistance=220 package=THT]
  R2 = Resistor [tolerance=±5% resistance=220 package=THT]
  R3 = Resistor [tolerance=±5% resistance=220 package=THT]
  Q1 = NPN-Transistor [package="TO92 [THT]"]
  Q2 = NPN-Transistor [package="TO92 [THT]"]
  Q3 = NPN-Transistor [package="TO92 [THT]"]
  RGB_Strip_LED1 = RGB Strip LED
  Power_plug1 = Power plug
  C1 = Electrolytic Capacitor [capacitance=1µF package="100 mil [THT, electrolytic]"]

nets:
  N1: U1.VCC, U1.ADC_0, U2.IN, C1.+
  GND: U1.GND, U1.GPIO_15, U2.ADJ, Q1.E, Q2.E, Q3.E, Power_plug1.GND, C1.-
  N2: U1.GPIO_16, R3.Pin_1
  N3: U1.GPIO_14, R2.Pin_1
  N4: U1.GPIO_12, R1.Pin_1
  N5: U2.OUT, RGB_Strip_LED1.Common_Connect, Power_plug1.VCC
  N6: Q1.C, RGB_Strip_LED1.Blue_Connect
  N7: Q2.C, RGB_Strip_LED1.Red_Connect
  N8: Q3.C, RGB_Strip_LED1.Green_Connect

custom parts:
  ESP8266 WiFi Module: Generic WiFi Module based on the ESP8266 with onboard PCB antenna and UART communications
  RGB Strip LED: A tri-color Strip LED with red, green and blue. Based on LED SMD 5050 RGB Pin order: common cathode - green - red - blue
