# Fritzing sketch Breadboard (saved by Fritzing 0.8.3b)
breadboards: 1

parts:
  U1 = ESP8266 WiFi Module [part_number=ESP8266]
  S1 = Pushbutton [package="[THT]"]
  Part1 = FTDI Basic Programmer
  R2 = Resistor [tolerance=±5% resistance=4.7k package=THT]
  KY-1 = Keyes Relay [package=THT]
  U2 = TLP621 [package=THT]
  R3 = Resistor [tolerance=±5% resistance=220 package=THT]
  C1 = Electrolytic Capacitor [capacitance=1µF package="100 mil [THT, electrolytic]"]
  Power_plug1 = Power plug

nets:
  N1: U1.RXD, Part1.TXO
  N2: U1.VCC, U1.CH_PD, Part1.POWER, R2.Pin_1
  N3: U1.GPIO_0, U1.RST, S1.Pin_1, S1.Pin_2
  N4: U1.GPIO_2, R2.Pin_0, R3.Pin_1
  GND: U1.GND, S1.Pin_3, S1.Pin_4, Part1.GND, KY-1.ground, U2.Pin_2, C1.-, Power_plug1.GND
  N5: U1.TXD, Part1.RXI
  N6: KY-1.signal, U2.Pin_3
  N7: KY-1.power, U2.Pin_4, C1.+, Power_plug1.VCC
  N8: U2.Pin_1, R3.Pin_0

notes:
  Note: My FTDI unit has both
  3.3V and 5V supply. If yours doesn't you will need a 5V supply as well for controlling the relay board like the power socket below.
  I also added a 100uf capacitor to the relay side to smooth out any power fluxuations from the relay board. Without this, the ESP8266 may crash occasionally. This makes it more stable.

custom parts:
  ESP8266 WiFi Module: Generic WiFi Module based on the ESP8266 with onboard PCB antenna and UART communications
  Keyes Relay: The Keyes 5V relay module is suitable for SCM development, home appliance control. It uses a 5V~12V TIL control signal which can control DC / AC signal.
